# Fritzing sketch SmartPot (saved by Fritzing 0.9.3b)
breadboards: 3

parts:
  MH-ET_LIVE_ESP32_DEVKIT1 = MH-ET LIVE ESP32 DEVKIT 38 pins
  DHT1 = DHT11 Humitidy and Temperature Sensor
  R1 = PHOTOCELL [package=photocell]
  Componente1 = Soil Moisture Sensor  # not connected
  R2 = Resistor [tolerance=±5% resistance=2k package=THT]
  R3 = Resistor [tolerance=±5% resistance=220 package=THT]
  Q1 = NPN-Transistor [package="TO92 [THT]"]
  Q2 = NPN-Transistor [package="TO92 [THT]"]
  Q3 = NPN-Transistor [package="TO92 [THT]"]
  R4 = Resistor [tolerance=±5% resistance=220 package="2010 [SMD]"]
  R5 = Resistor [tolerance=±5% resistance=220 package="2010 [SMD]"]
  R6 = Resistor [tolerance=±5% resistance=220 package=THT]
  LED1 = RGB LED (com. cathode, rgb) [package="5 mm [THT]"]
  R7 = Resistor [tolerance=±5% resistance=220 package="2010 [SMD]"]
  Q4 = NPN-Transistor [package="TO92 [THT]"]
  WATER_PUMP1 = water pump/motor  # not connected
  YwRobot_Power_Supply1 = YwRobot Breadboard Power Supply [part_number=545043]

nets:
  N1: MH-ET_LIVE_ESP32_DEVKIT1.IO21, R6.Pin_1
  N2: MH-ET_LIVE_ESP32_DEVKIT1.GND, R5.Pin_1
  N3: MH-ET_LIVE_ESP32_DEVKIT1.IO19, R4.Pin_1
  N4: MH-ET_LIVE_ESP32_DEVKIT1.IO5, R7.Pin_1
  N5: MH-ET_LIVE_ESP32_DEVKIT1.SD0, YwRobot_Power_Supply1.GND#11, YwRobot_Power_Supply1.GND#12
  N6: MH-ET_LIVE_ESP32_DEVKIT1.SCK, LED1.blue_anode, YwRobot_Power_Supply1.VCC#5, YwRobot_Power_Supply1.VCC#6
  N7: DHT1.DATA, DHT1.NULL, DHT1.GND, R1.P$2, R2.Pin_0, R3.Pin_1
  N8: R1.P$1, R2.Pin_1
  N9: Q1.E, R4.Pin_0
  N10: Q1.B, LED1.red_anode
  N11: Q1.C, Q2.C, Q3.C
  N12: Q2.E, R5.Pin_0
  N13: Q2.B, LED1.common_cathode
  N14: Q3.E, R6.Pin_0
  N15: Q3.B, LED1.green_anode
  N16: R7.Pin_0, Q4.B
  N17: Q4.E, YwRobot_Power_Supply1.VCC#9, YwRobot_Power_Supply1.VCC#10
  N18: YwRobot_Power_Supply1.GND#13, YwRobot_Power_Supply1.GND#14

notes:
  Interruttore a galleggiante

custom parts:
  MH-ET LIVE ESP32 DEVKIT 38 pins: http://mh.nodebb.com/topic/2/mh-et-live-esp32-devkit
  DHT11 Humitidy and Temperature Sensor: DHT11 Humidity and Temperature Sensor
  water pump/motor: WATER PUMP BY ARDUBLOCKTR
  YwRobot Breadboard Power Supply: The YwRobot Breadboard Power Supply (MB-V2) has two power rails; they can be 5V or 3V3. Power to the module can be provided through the female USB socket or through the A10 (female) 2.1mm power jack.
